// Logisim project NEW Project 4.1.circ as structural Verilog: 5 circuits, main circuit main
module main (
  input  in_1,
  input  in_2,
  input  in_3,
  output [22:0] out_4
);

  wire alu_1_zero_flag, and_1_out, clock_1_out, control_unit_1_alusrc, control_unit_1_branch,
       control_unit_1_jump, control_unit_1_memread, control_unit_1_memtoreg, control_unit_1_memwrite,
       control_unit_1_regdst, control_unit_1_regwrite;
  wire [1:0] control_unit_1_aluop;
  wire [2:0] alu_control_1_out_3;
  wire [4:0] multiplexer_1_out;
  wire [22:0] adder_1_out, bit_extender_1_out, bit_extender_2_out, bit_extender_3_out, multiplexer_2_out,
       multiplexer_3_out, multiplexer_4_out, multiplexer_5_out, PC_q, ram_1_data,
       register_file_1_read_data_1, register_file_1_read_data_2, rom_1_data;

  Clock clock_1 (.out(clock_1_out));
  Register #(.width(23)) PC (.D(multiplexer_4_out), .Q(PC_q), .clk(clock_1_out), .clr(in_2));  // open: en
  assign bit_extender_1_out = {{22{1'b0}}, 1'b1};  // Bit_Extender bit_extender_1
  Adder #(.width(23)) adder_1 (.a(bit_extender_1_out), .b(PC_q), .out(adder_1_out));  // open: cin, cout
  ROM #(.addrWidth(23), .dataWidth(23)) rom_1 (.addr(PC_q), .data(rom_1_data));  // open: sel
  assign bit_extender_2_out = {{3{1'b0}}, rom_1_data[19:0]};  // Bit_Extender bit_extender_2
  assign bit_extender_3_out = {{13{1'b0}}, rom_1_data[9:0]};  // Bit_Extender bit_extender_3
  Control_Unit control_unit_1 (
    .Opcode(rom_1_data[22:20]), .RegDst(control_unit_1_regdst), .ALUSrc(control_unit_1_alusrc),
    .MemToReg(control_unit_1_memtoreg), .RegWrite(control_unit_1_regwrite), .MemRead(control_unit_1_memread),
    .MemWrite(control_unit_1_memwrite), .Branch(control_unit_1_branch), .Jump(control_unit_1_jump),
    .ALUOp(control_unit_1_aluop));
  Multiplexer #(.width(5), .enable("false")) multiplexer_1 (
    .in0(rom_1_data[14:10]), .in1(rom_1_data[9:5]), .out(multiplexer_1_out), .sel(control_unit_1_regdst));
  ALU_Control alu_control_1 (.Funct(rom_1_data[2:0]), .ALUop(control_unit_1_aluop), .out_3(alu_control_1_out_3));
  Register_File register_file_1 (
    .Read_Register_1(rom_1_data[19:15]), .Write_Register(multiplexer_1_out),
    .Read_Register_2(rom_1_data[14:10]), .Write_Control(control_unit_1_regwrite),
    .Read_Data_1(register_file_1_read_data_1), .Read_Data_2(register_file_1_read_data_2), .Clear(in_3),
    .Write_Data(multiplexer_5_out), .in_5(clock_1_out));
  Multiplexer #(.width(23), .enable("false")) multiplexer_2 (
    .in0(register_file_1_read_data_2), .in1(bit_extender_3_out), .out(multiplexer_2_out),
    .sel(control_unit_1_alusrc));
  ALU alu_1 (
    .Shamt(rom_1_data[4:3]), .Zero_Flag(alu_1_zero_flag), .out_5(out_4), .A(register_file_1_read_data_1),
    .B(multiplexer_2_out), .s2s1s0(alu_control_1_out_3));
  and and_1 (and_1_out, control_unit_1_branch, alu_1_zero_flag);
  Multiplexer #(.width(23), .enable("false")) multiplexer_3 (
    .in0(adder_1_out), .in1(bit_extender_3_out), .out(multiplexer_3_out), .sel(and_1_out));
  Multiplexer #(.width(23), .enable("false")) multiplexer_4 (
    .in0(multiplexer_3_out), .in1(bit_extender_2_out), .out(multiplexer_4_out), .sel(control_unit_1_jump));
  RAM #(.addrWidth(23), .dataWidth(23), .bus("separate")) ram_1 (
    .addr(out_4), .din(register_file_1_read_data_2), .data(ram_1_data), .str(control_unit_1_memwrite),
    .clk(clock_1_out), .ld(control_unit_1_memread), .clr(in_1));  // open: sel
  Multiplexer #(.width(23), .enable("false")) multiplexer_5 (
    .in0(out_4), .in1(ram_1_data), .out(multiplexer_5_out), .sel(control_unit_1_memtoreg));

  // Notes on the sheet:
  //   contents of rom_1 (hex, n*v repeats v):
  //   600003 508802 10820 60 420003 600001
  //   op
  //   Rs
  //   Rt
  //   Rd
  //   Shamt
  //   Funct
endmodule

module ALU (
  input  [22:0] A,
  input  [22:0] B,
  input  [1:0] Shamt,
  input  [2:0] s2s1s0,
  output [22:0] out_5,
  output Zero_Flag
);

  wire comparator_1_lt;
  wire [4:0] bit_extender_1_out;
  wire [22:0] adder_1_out, and_1_out, bit_extender_2_out, nor_1_out, or_1_out, shifter_1_out, shifter_2_out,
       subtractor_1_out;

  assign bit_extender_1_out = {{3{1'b0}}, Shamt};  // Bit_Extender bit_extender_1
  assign and_1_out = A & B;  // AND_Gate and_1, 23 bits wide
  assign or_1_out = A | B;  // OR_Gate or_1, 23 bits wide
  assign nor_1_out = ~(A | B);  // NOR_Gate nor_1, 23 bits wide
  Comparator #(.width(23)) comparator_1 (.a(A), .b(B), .lt(comparator_1_lt));  // open: gt, eq
  Adder #(.width(23)) adder_1 (.a(A), .b(B), .out(adder_1_out));  // open: cin, cout
  Subtractor #(.width(23)) subtractor_1 (.a(A), .b(B), .out(subtractor_1_out));  // open: bin, bout
  assign bit_extender_2_out = {{22{1'b0}}, comparator_1_lt};  // Bit_Extender bit_extender_2
  Shifter #(.width(23)) shifter_1 (.in(A), .\dist (bit_extender_1_out), .out(shifter_1_out));
  Shifter #(.width(23), .shift("lr")) shifter_2 (.in(A), .\dist (bit_extender_1_out), .out(shifter_2_out));
  Multiplexer #(.select(3), .width(23), .enable("false")) multiplexer_1 (
    .in0(adder_1_out), .in1(subtractor_1_out), .in2(and_1_out), .in3(or_1_out), .in4(nor_1_out),
    .in5(bit_extender_2_out), .in6(shifter_1_out), .in7(shifter_2_out), .out(out_5), .sel(s2s1s0));
  nor nor_2 (Zero_Flag, out_5[0], out_5[1], out_5[2], out_5[3], out_5[4], out_5[5], out_5[6], out_5[7], out_5[8], out_5[9], out_5[10], out_5[11], out_5[12], out_5[13], out_5[14], out_5[15], out_5[16], out_5[17], out_5[18], out_5[19], out_5[20], out_5[21], out_5[22]);
endmodule

module Register_File (
  input  [4:0] Read_Register_1,
  input  [4:0] Write_Register,
  input  [4:0] Read_Register_2,
  input  Clear,
  input  in_5,
  input  Write_Control,
  input  [22:0] Write_Data,
  output [22:0] Read_Data_1,
  output [22:0] Read_Data_2
);

  wire and_1_out, and_2_out, and_3_out, and_4_out, and_5_out, and_6_out, and_7_out, and_8_out, and_9_out,
       and_10_out, and_11_out, and_12_out, and_13_out, and_14_out, and_15_out, and_16_out, and_17_out,
       and_18_out, and_19_out, and_20_out, and_21_out, and_22_out, and_23_out, decoder_1_out0,
       decoder_1_out1, decoder_1_out2, decoder_1_out3, decoder_1_out4, decoder_1_out5, decoder_1_out6,
       decoder_1_out7, decoder_1_out8, decoder_1_out9, decoder_1_out10, decoder_1_out11, decoder_1_out12,
       decoder_1_out13, decoder_1_out14, decoder_1_out15, decoder_1_out16, decoder_1_out17, decoder_1_out18,
       decoder_1_out19, decoder_1_out20, decoder_1_out21, decoder_1_out22;
  wire [22:0] R0_q, R1_q, R2_q, R3_q, R4_q, R5_q, R6_q, R7_q, R8_q, R9_q, R10_q, R11_q, R12_q, R13_q, R14_q,
       R15_q, R16_q, R17_q, R18_q, R19_q, R20_q, R21_q, R22_q;

  Decoder #(.select(5), .enable("false")) decoder_1 (
    .out0(decoder_1_out0), .out1(decoder_1_out1), .out2(decoder_1_out2), .out3(decoder_1_out3),
    .out4(decoder_1_out4), .out5(decoder_1_out5), .out6(decoder_1_out6), .out7(decoder_1_out7),
    .out8(decoder_1_out8), .out9(decoder_1_out9), .out10(decoder_1_out10), .out11(decoder_1_out11),
    .out12(decoder_1_out12), .out13(decoder_1_out13), .out14(decoder_1_out14), .out15(decoder_1_out15),
    .out16(decoder_1_out16), .out17(decoder_1_out17), .out18(decoder_1_out18), .out19(decoder_1_out19),
    .out20(decoder_1_out20), .out21(decoder_1_out21), .out22(decoder_1_out22), .sel(Write_Register));  // open: out23, out24, out25, out26, out27, out28, out29, out30, out31
  Register #(.width(23)) R0 (.D(Write_Data), .en(and_1_out), .Q(R0_q), .clk(in_5), .clr(Clear));
  and and_1 (and_1_out, decoder_1_out0, Write_Control);
  Register #(.width(23)) R1 (.D(Write_Data), .en(and_2_out), .Q(R1_q), .clk(in_5), .clr(Clear));
  and and_2 (and_2_out, decoder_1_out1, Write_Control);
  Register #(.width(23)) R2 (.D(Write_Data), .en(and_3_out), .Q(R2_q), .clk(in_5), .clr(Clear));
  and and_3 (and_3_out, decoder_1_out2, Write_Control);
  Register #(.width(23)) R3 (.D(Write_Data), .en(and_4_out), .Q(R3_q), .clk(in_5), .clr(Clear));
  and and_4 (and_4_out, decoder_1_out3, Write_Control);
  Register #(.width(23)) R4 (.D(Write_Data), .en(and_5_out), .Q(R4_q), .clk(in_5), .clr(Clear));
  and and_5 (and_5_out, decoder_1_out4, Write_Control);
  Register #(.width(23)) R5 (.D(Write_Data), .en(and_6_out), .Q(R5_q), .clk(in_5), .clr(Clear));
  and and_6 (and_6_out, decoder_1_out5, Write_Control);
  Register #(.width(23)) R6 (.D(Write_Data), .en(and_7_out), .Q(R6_q), .clk(in_5), .clr(Clear));
  and and_7 (and_7_out, decoder_1_out6, Write_Control);
  Register #(.width(23)) R7 (.D(Write_Data), .en(and_8_out), .Q(R7_q), .clk(in_5), .clr(Clear));
  and and_8 (and_8_out, decoder_1_out7, Write_Control);
  and and_9 (and_9_out, decoder_1_out8, Write_Control);
  and and_10 (and_10_out, decoder_1_out9, Write_Control);
  and and_11 (and_11_out, decoder_1_out10, Write_Control);
  and and_12 (and_12_out, decoder_1_out11, Write_Control);
  and and_13 (and_13_out, decoder_1_out12, Write_Control);
  and and_14 (and_14_out, decoder_1_out13, Write_Control);
  and and_15 (and_15_out, decoder_1_out14, Write_Control);
  and and_16 (and_16_out, decoder_1_out15, Write_Control);
  Register #(.width(23)) R8 (.D(Write_Data), .en(and_9_out), .Q(R8_q), .clk(in_5), .clr(Clear));
  Register #(.width(23)) R9 (.D(Write_Data), .en(and_10_out), .Q(R9_q), .clk(in_5), .clr(Clear));
  Register #(.width(23)) R10 (.D(Write_Data), .en(and_11_out), .Q(R10_q), .clk(in_5), .clr(Clear));
  Register #(.width(23)) R11 (.D(Write_Data), .en(and_12_out), .Q(R11_q), .clk(in_5), .clr(Clear));
  Register #(.width(23)) R12 (.D(Write_Data), .en(and_13_out), .Q(R12_q), .clk(in_5), .clr(Clear));
  Register #(.width(23)) R13 (.D(Write_Data), .en(and_14_out), .Q(R13_q), .clk(in_5), .clr(Clear));
  Register #(.width(23)) R14 (.D(Write_Data), .en(and_15_out), .Q(R14_q), .clk(in_5), .clr(Clear));
  Register #(.width(23)) R15 (.D(Write_Data), .en(and_16_out), .Q(R15_q), .clk(in_5), .clr(Clear));
  and and_17 (and_17_out, decoder_1_out16, Write_Control);
  and and_18 (and_18_out, decoder_1_out17, Write_Control);
  and and_19 (and_19_out, decoder_1_out18, Write_Control);
  and and_20 (and_20_out, decoder_1_out19, Write_Control);
  and and_21 (and_21_out, decoder_1_out20, Write_Control);
  and and_22 (and_22_out, decoder_1_out21, Write_Control);
  and and_23 (and_23_out, decoder_1_out22, Write_Control);
  Register #(.width(23)) R16 (.D(Write_Data), .en(and_17_out), .Q(R16_q), .clk(in_5), .clr(Clear));
  Register #(.width(23)) R17 (.en(and_18_out), .Q(R17_q), .clk(in_5), .clr(Clear));  // open: D
  Register #(.width(23)) R18 (.D(Write_Data), .en(and_19_out), .Q(R18_q), .clk(in_5), .clr(Clear));
  Register #(.width(23)) R19 (.D(Write_Data), .en(and_20_out), .Q(R19_q), .clk(in_5), .clr(Clear));
  Register #(.width(23)) R20 (.D(Write_Data), .en(and_21_out), .Q(R20_q), .clk(in_5), .clr(Clear));
  Register #(.width(23)) R21 (.D(Write_Data), .en(and_22_out), .Q(R21_q), .clk(in_5), .clr(Clear));
  Register #(.width(23)) R22 (.D(Write_Data), .en(and_23_out), .Q(R22_q), .clk(in_5), .clr(Clear));
  Multiplexer #(.select(5), .width(23), .enable("false")) multiplexer_1 (
    .in0(R0_q), .in1(R1_q), .in2(R2_q), .in3(R3_q), .in4(R4_q), .in5(R5_q), .in6(R6_q), .in7(R7_q),
    .in8(R8_q), .in9(R9_q), .in10(R10_q), .in11(R11_q), .in12(R12_q), .in13(R13_q), .in14(R14_q),
    .in15(R15_q), .in16(R16_q), .in17(R17_q), .in18(R18_q), .in19(R19_q), .in20(R20_q), .in21(R21_q),
    .in22(R22_q), .out(Read_Data_1), .sel(Read_Register_1));  // open: in23, in24, in25, in26, in27, in28, in29, in30, in31
  Multiplexer #(.select(5), .width(23), .enable("false")) multiplexer_2 (
    .in0(R0_q), .in1(R1_q), .in2(R2_q), .in3(R3_q), .in4(R4_q), .in5(R5_q), .in6(R6_q), .in7(R7_q),
    .in8(R8_q), .in9(R9_q), .in10(R10_q), .in11(R11_q), .in12(R12_q), .in13(R13_q), .in14(R14_q),
    .in15(R15_q), .in16(R16_q), .in17(R17_q), .in18(R18_q), .in19(R19_q), .in20(R20_q), .in21(R21_q),
    .in22(R22_q), .out(Read_Data_2), .sel(Read_Register_2));  // open: in23, in24, in25, in26, in27, in28, in29, in30, in31
endmodule

module Control_Unit (
  input  [2:0] Opcode,
  output RegDst,
  output ALUSrc,
  output MemToReg,
  output RegWrite,
  output MemRead,
  output MemWrite,
  output Branch,
  output Jump,
  output [1:0] ALUOp
);

  wire decoder_1_out2, decoder_1_out3, decoder_1_out4, decoder_1_out7;

  Decoder #(.select(3), .enable("false")) decoder_1 (
    .out0(ALUOp[1]), .out1(MemRead), .out2(decoder_1_out2), .out3(decoder_1_out3), .out4(decoder_1_out4),
    .out5(MemWrite), .out6(Jump), .out7(decoder_1_out7), .sel(Opcode));
  or or_1 (ALUSrc, MemRead, decoder_1_out2, MemWrite);
  or or_2 (RegWrite, ALUOp[1], MemRead, decoder_1_out2);
  or or_3 (Branch, decoder_1_out3, decoder_1_out4);
  or or_4 (ALUOp[0], decoder_1_out3, decoder_1_out4);

  assign MemToReg = MemRead;
  assign RegDst = ALUOp[1];
endmodule

module ALU_Control (
  input  [2:0] Funct,
  input  [1:0] ALUop,
  output [2:0] out_3
);

  wire and_3_out;

  and and_1 (out_3[2], ALUop[1], Funct[2]);
  and and_2 (out_3[1], ALUop[1], Funct[1]);
  and and_3 (and_3_out, ALUop[1], Funct[0]);
  or or_1 (out_3[0], and_3_out, ALUop[0]);
endmodule
